// Logisim project lab1.2.circ as structural Verilog: 1 circuit, main circuit cmos_or
module cmos_or (
  input  X,
  input  Y,
  output Z
);

  wire transistor_1_out, transistor_2_out;

  Transistor transistor_1 (.in(transistor_2_out), .out(transistor_1_out), .gate(X));
  Transistor transistor_2 (.in(Y), .out(transistor_2_out), .gate(Y));
  Transistor transistor_3 (.in(1'b0), .out(Y), .gate(X));
  Transistor transistor_4 (.in(Z), .out(transistor_1_out), .gate(Y));
  Transistor transistor_5 (.in(1'b0), .out(Z), .gate(Y));
  Transistor transistor_6 (.in(1'b0), .out(Y), .gate(Y));
  // also tied to VCC on the sheet: transistor_1_out

  // Notes on the sheet:
  //   输入引脚
  //   请勿增加、删除引脚，用隧道标签构建电路
  //   请勿更改电路封装外观
  //   提示：使用三极管组件实现或门电路，禁止直接使用逻辑门组件。
  //   输出引脚
endmodule
